// Logisim project auto_arm_proj.circ as structural Verilog: 6 circuits, main circuit auto_arm_simulation
module auto_arm_simulation (
);

  wire auto_arm_top_1_dest_blue_o, auto_arm_top_1_dest_init_o, auto_arm_top_1_dest_red_o,
       auto_arm_top_1_drop_o, auto_arm_top_1_move_o, auto_arm_top_1_scan_o, auto_arm_top_1_throw_o,
       clk_i_out, tclconsolereds_1_p23, tclconsolereds_1_p26;
  wire [1:0] tclconsolereds_1_p24;

  Clock clk_i (.out(clk_i_out));
  Clock sysclk ();  // open: out
  auto_arm_top auto_arm_top_1 (
    .ready_i(tclconsolereds_1_p23), .color_i(tclconsolereds_1_p24), .clk_i(clk_i_out),
    .reset_i(tclconsolereds_1_p26), .scan_o(auto_arm_top_1_scan_o), .throw_o(auto_arm_top_1_throw_o),
    .move_o(auto_arm_top_1_move_o), .dest_red_o(auto_arm_top_1_dest_red_o),
    .dest_blue_o(auto_arm_top_1_dest_blue_o), .dest_init_o(auto_arm_top_1_dest_init_o),
    .drop_o(auto_arm_top_1_drop_o));
  // TclConsoleReds #(.filePath("console\\console_auto_arm.tcl")) tclconsolereds_1: pin names not known; wires that end beside it: 4'b0000, 4'b0000, auto_arm_top_1_scan_o, auto_arm_top_1_throw_o, auto_arm_top_1_move_o, auto_arm_top_1_dest_red_o, auto_arm_top_1_dest_blue_o, auto_arm_top_1_dest_init_o, auto_arm_top_1_drop_o, 1'b0, 1'b0, 1'b0, 1'b0, 1'b0, 1'b0, 1'b0, 1'b0, 1'b0, {16{1'b0}}, {16{1'b0}}, {8{1'b0}}, clk_i_out, tclconsolereds_1_p23, tclconsolereds_1_p24[0], tclconsolereds_1_p24[1], tclconsolereds_1_p26

  // Notes on the sheet:
  //   Attention, votre version de Logisim
  //   ne contient pas de tracker. Si vous
  //   enregistrez votre projet, toutes les
  //   informations du tracker seront
  //   définitivement effacées.
endmodule

module auto_arm_top (
  input  ready_i,
  input  [1:0] color_i,
  input  clk_i,
  input  reset_i,
  output scan_o,
  output throw_o,
  output move_o,
  output dest_red_o,
  output dest_blue_o,
  output dest_init_o,
  output drop_o
);

  wire timer_1_end_timer_o;

  timer timer_1 (.nReset(move_o), .clk(clk_i), .end_timer_o(timer_1_end_timer_o));
  MSS mss_1 (
    .ready_i(ready_i), .color_i(color_i), .timer(timer_1_end_timer_o), .reset(reset_i), .clk(reset_i),
    .outputs({drop_o, dest_init_o, dest_blue_o, dest_red_o, move_o, throw_o, scan_o}));

  // Notes on the sheet:
  //   Attention, votre version de Logisim
  //   ne contient pas de tracker. Si vous
  //   enregistrez votre projet, toutes les
  //   informations du tracker seront
  //   définitivement effacées.
endmodule

module timer (
  input  nReset,
  input  clk,
  output end_timer_o
);

  wire not_1_out;

  Counter #(.width(2), .max('h2)) counter_1 (
    .clr(not_1_out), .clk(clk), .carry(end_timer_o));  // open: load, up, count, D, Q
  not not_1 (not_1_out, nReset);

  // Notes on the sheet:
  //   Attention, votre version de Logisim
  //   ne contient pas de tracker. Si vous
  //   enregistrez votre projet, toutes les
  //   informations du tracker seront
  //   définitivement effacées.
endmodule

module MSS (
  input  ready_i,
  input  [1:0] color_i,
  input  timer,
  input  reset,
  input  clk,
  output [6:0] outputs
);

  wire [6:0] d_ff_6_q, decodeur_etat_1_state_fut;

  decodeur_etat decodeur_etat_1 (
    .state_pres(d_ff_6_q), .ready_i(ready_i), .color_i(color_i), .timer(timer), .reset(reset),
    .state_fut(decodeur_etat_1_state_fut));
  D_Flip_Flop d_ff_1 (.D(decodeur_etat_1_state_fut[5]), .clk(clk), .Q(d_ff_6_q[5]), .preset(reset));  // open: Qn, reset
  D_Flip_Flop d_ff_2 (.D(decodeur_etat_1_state_fut[4]), .clk(clk), .Q(d_ff_6_q[4]), .preset(reset));  // open: Qn, reset
  D_Flip_Flop d_ff_3 (.D(decodeur_etat_1_state_fut[3]), .clk(clk), .Q(d_ff_6_q[3]), .preset(reset));  // open: Qn, reset
  D_Flip_Flop d_ff_4 (.D(decodeur_etat_1_state_fut[2]), .clk(clk), .Q(d_ff_6_q[2]), .preset(reset));  // open: Qn, reset
  D_Flip_Flop d_ff_5 (.D(decodeur_etat_1_state_fut[1]), .clk(clk), .Q(d_ff_6_q[1]), .preset(reset));  // open: Qn, reset
  D_Flip_Flop d_ff_6 (.D(decodeur_etat_1_state_fut[0]), .clk(clk), .Q(d_ff_6_q[0]), .preset(1'b1));  // open: Qn, reset
  D_Flip_Flop d_ff_7 (.D(decodeur_etat_1_state_fut[6]), .clk(clk), .Q(d_ff_6_q[6]), .preset(reset));  // open: Qn, reset
  decodeur_sorties decodeur_sorties_1 (.state_i(d_ff_6_q), .outputs(outputs));

  // Notes on the sheet:
  //   Attention, votre version de Logisim
  //   ne contient pas de tracker. Si vous
  //   enregistrez votre projet, toutes les
  //   informations du tracker seront
  //   définitivement effacées.
endmodule

module decodeur_etat (
  input  [6:0] state_pres,
  input  ready_i,
  input  [1:0] color_i,
  input  timer,
  input  reset,
  output [6:0] state_fut
);

  wire and_1_out, and_2_out, and_3_out, and_4_out, and_5_out, and_6_out, and_7_out, and_8_out, and_9_out,
       and_10_out, and_12_out, not_color0, not_color1, not_ready, not_timer, or_1_out;

  not not_1 (not_ready, ready_i);
  not not_2 (not_color0, color_i[0]);
  not not_3 (not_color1, color_i[1]);
  not not_4 (not_timer, timer);
  and and_1 (and_1_out, state_pres[0], not_ready);
  and and_2 (and_2_out, state_pres[6], timer);
  and and_3 (and_3_out, state_pres[0], ready_i);
  and and_4 (and_4_out, state_pres[1], color_i[0], color_i[1]);
  and and_5 (and_5_out, state_pres[1], color_i[0], not_color1);
  and and_6 (and_6_out, state_pres[3], not_timer);
  and and_7 (and_7_out, state_pres[1], color_i[1], not_color0);
  and and_8 (and_8_out, state_pres[4], not_timer);
  and and_9 (and_9_out, state_pres[3], timer);
  and and_10 (and_10_out, state_pres[4], timer);
  or or_1 (or_1_out, and_1_out, state_pres[2], and_2_out);
  or or_2 (state_fut[0], or_1_out, reset);
  or or_3 (state_fut[1], and_3_out, and_4_out);
  and and_11 (state_fut[2], state_pres[1], not_color0, not_color1);
  or or_4 (state_fut[3], and_5_out, and_6_out);
  or or_5 (state_fut[4], and_7_out, and_8_out);
  or or_6 (state_fut[5], and_9_out, and_10_out);
  and and_12 (and_12_out, state_pres[6], not_timer);
  or or_7 (state_fut[6], state_pres[5], and_12_out);

  // Other names for the same wires on the sheet: color0 = color_i[0]; color1 = color_i[1]; ready = ready_i;
  //   E0 = state_fut[0]; E1 = state_fut[1]; E2 = state_fut[2]; E3 = state_fut[3]; E4 = state_fut[4];
  //   E5 = state_fut[5]; E6 = state_fut[6]; Q0 = state_pres[0]; Q1 = state_pres[1]; Q2 = state_pres[2];
  //   Q3 = state_pres[3]; Q4 = state_pres[4]; Q5 = state_pres[5]; Q6 = state_pres[6]

  // Notes on the sheet:
  //   Attention, votre version de Logisim
  //   ne contient pas de tracker. Si vous
  //   enregistrez votre projet, toutes les
  //   informations du tracker seront
  //   définitivement effacées.
endmodule

module decodeur_sorties (
  input  [6:0] state_i,
  output [6:0] outputs
);

  wire [2:2] or_1_out;

  or or_1 (or_1_out[2], state_i[3], state_i[4], state_i[6]);
  Multiplexer #(.width(7), .enable("false")) multiplexer_1 (
    .in0({7{1'b0}}), .in1({state_i[5], state_i[6], state_i[4:3], or_1_out[2], state_i[2:1]}), .out(outputs),
    .sel(state_i[0]));

  // Notes on the sheet:
  //   Attention, votre version de Logisim
  //   ne contient pas de tracker. Si vous
  //   enregistrez votre projet, toutes les
  //   informations du tracker seront
  //   définitivement effacées.
endmodule
